# Fritzing sketch thermometer (saved by Fritzing 0.9.6b)
breadboards: 1

parts:
  Part1 = Arduino Uno (Rev3)
  LED1 = LED - 5mm [color="Red (633nm)" current=0.030 package="5 mm [THT]"]  # not connected
  LED2 = LED - 5mm [color="Green (555nm)" current=0.030 package="5 mm [THT]"]
  LED3 = LED - 5mm [color="Blue (430nm)" current=0.030 package="5 mm [THT]"]
  R1 = Resistor [tolerance=±5% power=0.25 resistance=220 package=THT]
  R2 = Resistor [tolerance=±5% power=0.25 resistance=220 package=THT]
  R3 = Resistor [tolerance=±5% power=0.25 resistance=220 package=THT]
  Q1 = NPN-Transistor [package="TO92 [THT]"]
  R4 = Trimmer Potentiometer [maximum_resistance=10kΩ package=THT]
  LCD1 = LCD screen
  R5 = Resistor [tolerance=±5% power=0.25 resistance=220 package=THT]

nets:
  N1: Part1.A0, Q1.B
  N2: Part1.D8, LED2.anode
  N3: Part1.D11_PWM/MOSI, LCD1.E
  N4: Part1.D12/MISO, LCD1.RS
  N5: Part1.D2, LCD1.DB7
  N6: Part1.D3_PWM, LCD1.DB6
  N7: Part1.D4, LCD1.DB5
  N8: Part1.D5_PWM, LCD1.DB4
  N9: Part1.D7, LED3.anode
  5V: Part1.5V, Q1.E, R4.leg1, LCD1.VDD, R5.Pin_0
  GND: Part1.GND, R1.Pin_0, R2.Pin_0, R3.Pin_0, Q1.C, R4.leg2, LCD1.VSS, LCD1.R/W, LCD1.LED-
  N10: LED2.cathode, R1.Pin_1
  N11: LED3.cathode, R3.Pin_1
  N12: R4.wiper, LCD1.V0
  N13: LCD1.LED+, R5.Pin_1
